// Digital circuit ALU.dig as structural Verilog
module ALU (
  input  [2:0] in_1,
  input  [7:0] in_2,
  input  [7:0] in_3
);

  wire And, Mult, OR, S_L, S_R, Soma, Sub, Xor;
  wire [7:0] Out, Out_1, Out_2, Out_3, Out_4, Out_5, Out_6, Out_7, Out_8;

  LED led_1 (.in(in_3[7]));
  LED led_2 (.in(in_3[6]));
  LED led_3 (.in(in_3[5]));
  LED led_4 (.in(in_3[4]));
  LED led_5 (.in(in_3[3]));
  Seven_Seg_Hex seven_seg_hex_1 (.d(in_3[7:4]), .dp(1'b0));
  Seletor seletor_1 (
    .IN(in_1), .Soma(Soma), .Sub(Sub), .Mult(Mult), .Shift_R(S_R), .Shift_l(S_L), .And(And), .Or(OR),
    .Xor(Xor));
  LED led_6 (.in(in_3[2]));
  LED led_7 (.in(in_3[1]));
  Seven_Seg_Hex seven_seg_hex_2 (.d(in_3[3:0]), .dp(1'b0));
  LED led_8 (.in(in_3[0]));
  LED led_9 (.in(in_2[7]));
  LED led_10 (.in(in_2[6]));
  Seven_Seg_Hex seven_seg_hex_3 (.d(in_2[7:4]), .dp(1'b0));
  LED led_11 (.in(in_2[5]));
  LED led_12 (.in(in_2[4]));
  Seven_Seg_Hex seven_seg_hex_4 (.d(in_2[3:0]), .dp(1'b0));
  Somador_8bits somador_8bits_1 (
    .In1_8bits(in_3), .In2_8bits(in_2), .Enable(Soma), .Cin(1'b0), .S_8bits(Out_1));  // open: Cout
  Shift_R shift_r_1 (.In_8bits(in_3), .Enable(S_R), .Out_8bits(Out_4));
  AND and_1 (.IN1(in_3), .IN2(in_2), .Enable(And), .Out(Out_6));
  LED led_13 (.in(in_2[3]));
  LED led_14 (.in(in_2[2]));
  LED led_15 (.in(in_2[1]));
  LED led_16 (.in(in_2[0]));
  Subtrator subtrator_1 (.In1_8bits(in_3), .In2_8bits(in_2), .Enable(Sub), .Out(Out_2));
  Shift_L shift_l_1 (.In_8bits(in_2), .Enable(S_L), .Out_8bits(Out_5));
  OR or_1 (.IN1(in_3), .IN2(in_2), .Enable(OR), .Out(Out_7));
  LED led_17 (.in(Out[7]));
  LED led_18 (.in(Out[6]));
  Seven_Seg_Hex seven_seg_hex_5 (.d(Out[7:4]), .dp(1'b0));
  LED led_19 (.in(Out[5]));
  LED led_20 (.in(Out[4]));
  Seven_Seg_Hex seven_seg_hex_6 (.d(Out[3:0]), .dp(1'b0));
  LED led_21 (.in(Out[3]));
  LED led_22 (.in(Out[2]));
  LED led_23 (.in(Out[1]));
  LED led_24 (.in(Out[0]));
  Multiplicador multiplicador_1 (.In2_8bits(in_3), .In1_8bits(in_2), .Enable(Mult), .Out_8bits(Out_3));
  XOR xor_1 (.IN1(in_3), .IN2(in_2), .Enable(Xor), .Out(Out_8));
  assign Out = Out_1 ^ Out_2 ^ Out_3 ^ Out_4 ^ Out_5 ^ Out_6 ^ Out_7 ^ Out_8;  // XOr xor_2, 8 bits wide

  // Other names for the same wires on the sheet: A[7:0] = in_3; B[7:0] = in_2

  // Notes on the sheet:
  //   Binario primeiro numero
  //   Hexa primeiro numero
  //   Seletor
  //   Binario segundo numero
  //   Hexa segundo numero
  //   Operações
  //   Binario resultado
  //   Hexa resultado
  //   Out_puts
endmodule
