// Digital circuit AND.dig as structural Verilog
module AND (
  input  [7:0] IN1,
  input  [7:0] IN2,
  input  Enable,
  output [7:0] Out
);

  wire [7:0] enable_1_out1_8bits, enable_1_out2_8bits;

  Enable enable_1 (
    .In1_8bits(IN1), .Enable(Enable), .In2_8bits(IN2), .Out1_8bits(enable_1_out1_8bits),
    .Out2_8bits(enable_1_out2_8bits));
  assign Out = enable_1_out1_8bits & enable_1_out2_8bits;  // And and_1, 8 bits wide
endmodule
