// Digital circuit Multiplicador.dig as structural Verilog
module Multiplicador (
  input  [7:0] In2_8bits,
  input  [7:0] In1_8bits,
  input  Enable,
  output [7:0] Out_8bits
);

  wire A0, A1, A2, A3, B0, B1, B2, B3;
  wire [2:0] and_10_out;
  wire [3:0] and_1_out, and_2_out, and_3_out, somador_4bits_1_p3, somador_4bits_2_p3;
  wire [7:4] enable_1_out1_8bits, enable_1_out2_8bits;

  Enable enable_1 (
    .In1_8bits(In1_8bits), .Enable(Enable), .In2_8bits(In2_8bits),
    .Out1_8bits({enable_1_out1_8bits, A3, A2, A1, A0}), .Out2_8bits({enable_1_out2_8bits, B3, B2, B1, B0}));
  and and_1 (and_1_out[3], A3, B1);
  and and_2 (and_2_out[3], A3, B2);
  and and_3 (and_3_out[3], A3, B3);
  and and_4 (and_1_out[2], A2, B1);
  and and_5 (and_2_out[2], A2, B2);
  and and_6 (and_3_out[2], A2, B3);
  and and_7 (and_1_out[1], A1, B1);
  and and_8 (and_2_out[1], A1, B2);
  and and_9 (and_3_out[1], A1, B3);
  and and_10 (and_10_out[2], A3, B0);
  and and_11 (and_1_out[0], A0, B1);
  and and_12 (and_2_out[0], A0, B2);
  and and_13 (and_3_out[0], A0, B3);
  and and_14 (and_10_out[1], A2, B0);
  // Somador_4bits somador_4bits_1: pin names not known; wires that end beside it: 1'b0, and_1_out, somador_4bits_1_p3[3], {1'b0, and_10_out}, {somador_4bits_1_p3[2:0], Out_8bits[1]}
  // Somador_4bits somador_4bits_2: pin names not known; wires that end beside it: 1'b0, and_2_out, somador_4bits_2_p3[3], somador_4bits_1_p3, {somador_4bits_2_p3[2:0], Out_8bits[2]}
  // Somador_4bits somador_4bits_3: pin names not known; wires that end beside it: 1'b0, and_3_out, Out_8bits[7], somador_4bits_2_p3, Out_8bits[6:3]
  and and_15 (and_10_out[0], A1, B0);
  and and_16 (Out_8bits[0], A0, B0);
endmodule
