// Digital circuit Seletor.dig as structural Verilog
module Seletor (
  input  [2:0] IN,
  output Soma,
  output Sub,
  output Mult,
  output Shift_R,
  output Shift_l,
  output And,
  output Or,
  output Xor
);

  wire not_1_out, not_2_out, not_3_out;

  not not_1 (not_1_out, IN[0]);
  not not_2 (not_2_out, IN[1]);
  not not_3 (not_3_out, IN[2]);
  and and_1 (Soma, not_1_out, not_2_out, not_3_out);
  and and_2 (Sub, IN[0], not_2_out, not_3_out);
  and and_3 (Mult, not_1_out, IN[1], not_3_out);
  and and_4 (Shift_R, IN[0], IN[1], not_3_out);
  and and_5 (Shift_l, not_1_out, not_2_out, IN[2]);
  and and_6 (And, IN[0], not_2_out, IN[2]);
  and and_7 (Or, not_1_out, IN[1], IN[2]);
  and and_8 (Xor, IN[0], IN[1], IN[2]);
endmodule
