// Digital circuit Shift_L.dig as structural Verilog
module Shift_L (
  input  [7:0] In_8bits,
  input  Enable,
  output [7:0] Out_8bits
);

  wire [7:7] enable_1_out1_8bits;

  Enable enable_1 (
    .In1_8bits(In_8bits), .Enable(Enable), .In2_8bits(In_8bits),
    .Out1_8bits({enable_1_out1_8bits[7], Out_8bits[7:1]}));  // open: Out2_8bits

  assign Out_8bits[0] = 1'b0;
endmodule
