// Digital circuit Shift_R.dig as structural Verilog
module Shift_R (
  input  [7:0] In_8bits,
  input  Enable,
  output [7:0] Out_8bits
);

  wire [0:0] enable_1_out1_8bits;

  Enable enable_1 (
    .In1_8bits(In_8bits), .Enable(Enable), .In2_8bits(In_8bits),
    .Out1_8bits({Out_8bits[6:0], enable_1_out1_8bits[0]}));  // open: Out2_8bits

  assign Out_8bits[7] = 1'b0;
endmodule
