// Digital circuit Somador_1bit.dig as structural Verilog
module Somador_1bit (
  input  A,
  input  B,
  input  In,
  output D,
  output Out
);

  wire and_1_out, and_2_out, and_3_out, and_4_out, and_5_out, and_6_out, and_7_out, and_8_out, not_1_out,
       not_2_out, not_3_out, or_1_out, or_2_out, or_3_out, or_4_out;

  not not_1 (not_1_out, A);
  not not_2 (not_2_out, B);
  not not_3 (not_3_out, In);
  and and_1 (and_1_out, not_1_out, not_2_out, In);
  and and_2 (and_2_out, A, not_2_out, not_3_out);
  and and_3 (and_3_out, not_1_out, B, not_3_out);
  and and_4 (and_4_out, A, B, In);
  and and_5 (and_5_out, A, not_2_out, In);
  and and_6 (and_6_out, not_1_out, B, In);
  and and_7 (and_7_out, A, B, not_3_out);
  and and_8 (and_8_out, A, B, In);
  or or_1 (or_1_out, and_1_out, and_2_out);
  or or_2 (or_2_out, and_3_out, and_4_out);
  or or_3 (or_3_out, and_5_out, and_6_out);
  or or_4 (or_4_out, and_7_out, and_8_out);
  or or_5 (D, or_1_out, or_2_out);
  or or_6 (Out, or_3_out, or_4_out);
endmodule
