// Digital circuit Somador_4bits.dig as structural Verilog
module Somador_4bits (
  input  [3:0] In2_4bits,
  input  [3:0] In1_4bits,
  input  Cin,
  output [3:0] Out_4bits,
  output [3:0] Cout
);

  wire somador_1bit_1_out, somador_1bit_2_out, somador_1bit_3_out;

  Somador_1bit somador_1bit_1 (
    .A(In1_4bits[0]), .B(In2_4bits[0]), .In(Cin), .D(Out_4bits[0]), .Out(somador_1bit_1_out));
  Somador_1bit somador_1bit_2 (
    .A(In1_4bits[1]), .B(In2_4bits[1]), .In(somador_1bit_1_out), .D(Out_4bits[1]), .Out(somador_1bit_2_out));
  Somador_1bit somador_1bit_3 (
    .A(In1_4bits[2]), .B(In2_4bits[2]), .In(somador_1bit_2_out), .D(Out_4bits[2]), .Out(somador_1bit_3_out));
  // Somador_1bit somador_1bit_4: pin names not known; wires that end beside it: In1_4bits[3], In2_4bits[3], somador_1bit_3_out, Out_4bits[3], Cout
  LED led_1 (.in(Out_4bits[0]));
  LED led_2 (.in(Out_4bits[1]));
  LED led_3 (.in(Out_4bits[2]));
  LED led_4 (.in(Out_4bits[3]));
endmodule
