// Digital circuit Somador_8bits.dig as structural Verilog
module Somador_8bits (
  input  [7:0] In1_8bits,
  input  [7:0] In2_8bits,
  input  Enable,
  input  Cin,
  output [7:0] S_8bits,
  output Cout
);

  wire somador_1bit_1_out, somador_1bit_2_out, somador_1bit_3_out, somador_1bit_4_out, somador_1bit_5_out,
       somador_1bit_6_out, somador_1bit_7_out;
  wire [7:0] enable_1_out1_8bits, enable_1_out2_8bits;

  Enable enable_1 (
    .In1_8bits(In1_8bits), .Enable(Enable), .In2_8bits(In2_8bits), .Out1_8bits(enable_1_out1_8bits),
    .Out2_8bits(enable_1_out2_8bits));
  Somador_1bit somador_1bit_1 (
    .A(enable_1_out1_8bits[0]), .B(enable_1_out2_8bits[0]), .In(Cin), .D(S_8bits[0]), .Out(somador_1bit_1_out));
  Somador_1bit somador_1bit_2 (
    .A(enable_1_out1_8bits[1]), .B(enable_1_out2_8bits[1]), .In(somador_1bit_1_out), .D(S_8bits[1]),
    .Out(somador_1bit_2_out));
  Somador_1bit somador_1bit_3 (
    .A(enable_1_out1_8bits[2]), .B(enable_1_out2_8bits[2]), .In(somador_1bit_2_out), .D(S_8bits[2]),
    .Out(somador_1bit_3_out));
  Somador_1bit somador_1bit_4 (
    .A(enable_1_out1_8bits[3]), .B(enable_1_out2_8bits[3]), .In(somador_1bit_3_out), .D(S_8bits[3]),
    .Out(somador_1bit_4_out));
  Somador_1bit somador_1bit_5 (
    .A(enable_1_out1_8bits[4]), .B(enable_1_out2_8bits[4]), .In(somador_1bit_4_out), .D(S_8bits[4]),
    .Out(somador_1bit_5_out));
  Somador_1bit somador_1bit_6 (
    .A(enable_1_out1_8bits[5]), .B(enable_1_out2_8bits[5]), .In(somador_1bit_5_out), .D(S_8bits[5]),
    .Out(somador_1bit_6_out));
  Somador_1bit somador_1bit_7 (
    .A(enable_1_out1_8bits[6]), .B(enable_1_out2_8bits[6]), .In(somador_1bit_6_out), .D(S_8bits[6]),
    .Out(somador_1bit_7_out));
  Somador_1bit somador_1bit_8 (
    .A(enable_1_out1_8bits[7]), .B(enable_1_out2_8bits[7]), .In(somador_1bit_7_out), .D(S_8bits[7]),
    .Out(Cout));
  LED led_1 (.in(S_8bits[0]));
  LED led_2 (.in(S_8bits[1]));
  LED led_3 (.in(S_8bits[2]));
  LED led_4 (.in(S_8bits[3]));
  LED led_5 (.in(S_8bits[4]));
  LED led_6 (.in(S_8bits[5]));
  LED led_7 (.in(S_8bits[6]));
  LED led_8 (.in(S_8bits[7]));
endmodule
