// Digital circuit Subtrator.dig as structural Verilog
module Subtrator (
  input  [7:0] In1_8bits,
  input  [7:0] In2_8bits,
  input  Enable,
  output [7:0] Out
);

  wire [7:0] not_1_out, somador_8bits_1_s_8bits;

  assign not_1_out = ~In2_8bits;  // Not not_1, 8 bits wide
  Somador_8bits somador_8bits_1 (
    .In1_8bits(8'h1), .In2_8bits(not_1_out), .Enable(Enable), .Cin(1'b0), .S_8bits(somador_8bits_1_s_8bits));  // open: Cout
  Somador_8bits somador_8bits_2 (
    .In1_8bits(In1_8bits), .In2_8bits(somador_8bits_1_s_8bits), .Enable(Enable), .Cin(1'b0), .S_8bits(Out));  // open: Cout

  // Other names for the same wires on the sheet: A[7:0] = In1_8bits; B[7:0] = In2_8bits
endmodule
