// Digital circuit Enable.dig as structural Verilog
module Enable (
  input  [7:0] In1_8bits,
  input  Enable,
  input  [7:0] In2_8bits,
  output [7:0] Out1_8bits,
  output [7:0] Out2_8bits
);

  and and_1 (Out1_8bits[0], In1_8bits[0], Enable);
  and and_2 (Out1_8bits[1], In1_8bits[1], Enable);
  and and_3 (Out1_8bits[2], In1_8bits[2], Enable);
  and and_4 (Out1_8bits[3], In1_8bits[3], Enable);
  and and_5 (Out1_8bits[4], In1_8bits[4], Enable);
  and and_6 (Out1_8bits[5], In1_8bits[5], Enable);
  and and_7 (Out1_8bits[6], In1_8bits[6], Enable);
  and and_8 (Out1_8bits[7], In1_8bits[7], Enable);
  and and_9 (Out2_8bits[0], In2_8bits[0], Enable);
  and and_10 (Out2_8bits[1], In2_8bits[1], Enable);
  and and_11 (Out2_8bits[2], In2_8bits[2], Enable);
  and and_12 (Out2_8bits[3], In2_8bits[3], Enable);
  and and_13 (Out2_8bits[4], In2_8bits[4], Enable);
  and and_14 (Out2_8bits[5], In2_8bits[5], Enable);
  and and_15 (Out2_8bits[6], In2_8bits[6], Enable);
  and and_16 (Out2_8bits[7], In2_8bits[7], Enable);
endmodule
