// Digital circuit Shift_L.dig as structural Verilog
module Shift_L (
  input  [7:0] In_8bits,
  output [7:0] Out_8bits
);

  // Pins of 1 and 8 bits meet at In_8bits
  // Pins of 1 and 8 bits meet at {In_8bits[6:0], 1'b0}

  assign Out_8bits = {In_8bits[6:0], 1'b0};
endmodule
