// Digital circuit Shift_R.dig as structural Verilog
module Shift_R (
  input  [7:0] In_8bits,
  output [7:0] Out_8bits
);

  // Pins of 1 and 8 bits meet at In_8bits
  // Pins of 1 and 8 bits meet at {1'b0, In_8bits[7:1]}

  assign Out_8bits = {1'b0, In_8bits[7:1]};
endmodule
