// Digital circuit Somador_8bits.dig as structural Verilog
module Somador_8bits (
  input  [7:0] In1_8bits,
  input  [7:0] In2_8bits,
  input  Enable,
  output [7:0] S_8bits
);

  wire somador_1_p5, somador_2_p5, somador_3_p5, somador_4_p5, somador_5_p5, somador_6_p5, somador_7_p5,
       somador_8_p5;
  wire [7:0] enable_1_out1_8bits, enable_1_out2_8bits;

  Enable enable_1 (
    .In1_8bits(In1_8bits), .Enable(Enable), .In2_8bits(In2_8bits), .Out1_8bits(enable_1_out1_8bits),
    .Out2_8bits(enable_1_out2_8bits));
  // Somador somador_1: pin names not known; wires that end beside it: enable_1_out1_8bits[0], enable_1_out2_8bits[0], 1'b0, S_8bits[0], somador_1_p5
  // Somador somador_2: pin names not known; wires that end beside it: enable_1_out1_8bits[1], enable_1_out2_8bits[1], somador_1_p5, S_8bits[1], somador_2_p5
  // Somador somador_3: pin names not known; wires that end beside it: enable_1_out1_8bits[2], enable_1_out2_8bits[2], somador_2_p5, S_8bits[2], somador_3_p5
  // Somador somador_4: pin names not known; wires that end beside it: enable_1_out1_8bits[3], enable_1_out2_8bits[3], somador_3_p5, S_8bits[3], somador_4_p5
  // Somador somador_5: pin names not known; wires that end beside it: enable_1_out1_8bits[4], enable_1_out2_8bits[4], somador_4_p5, S_8bits[4], somador_5_p5
  // Somador somador_6: pin names not known; wires that end beside it: enable_1_out1_8bits[5], enable_1_out2_8bits[5], somador_5_p5, S_8bits[5], somador_6_p5
  // Somador somador_7: pin names not known; wires that end beside it: enable_1_out1_8bits[6], enable_1_out2_8bits[6], somador_6_p5, S_8bits[6], somador_7_p5
  // Somador somador_8: pin names not known; wires that end beside it: enable_1_out1_8bits[7], enable_1_out2_8bits[7], somador_7_p5, S_8bits[7], somador_8_p5
  LED led_1 (.in(somador_8_p5));
  LED led_2 (.in(S_8bits[0]));
  LED led_3 (.in(S_8bits[1]));
  LED led_4 (.in(S_8bits[2]));
  LED led_5 (.in(S_8bits[3]));
  LED led_6 (.in(S_8bits[4]));
  LED led_7 (.in(S_8bits[5]));
  LED led_8 (.in(S_8bits[6]));
  LED led_9 (.in(S_8bits[7]));
endmodule
